# Fritzing sketch CameraTrapArduinoPhase2 (saved by Fritzing 0.9.3b)
breadboards: 1

parts:
  Part1 = Arduino Uno (Rev3)
  IR_LED = TSUS5402 [package=TSUS5402]
  R27 = 10 Ω Resistor [package=THT]
  R10 = 10 Ω Resistor [package=THT]
  R2200 = 27 Ω Resistor [package=THT]
  PN2222A = NPN-Transistor [package="TO92 [THT]"]
  HC-SR501_Motion_Sensor = HC-SR501 Body Sensor Module

nets:
  N1: Part1.D3_PWM, R2200.Pin_0
  N2: Part1.D7, HC-SR501_Motion_Sensor.OUT
  5V: Part1.5V, R27.Pin_0, HC-SR501_Motion_Sensor.VCC
  GND: Part1.GND, PN2222A.E, HC-SR501_Motion_Sensor.GND
  N3: IR_LED.A, R10.Pin_0
  N4: IR_LED.C, PN2222A.C
  N5: R27.Pin_1, R10.Pin_1
  N6: R2200.Pin_1, PN2222A.B

custom parts:
  TSUS5402: Through-hole side-firing 950nm IR LED
  10 Ω Resistor: A generic resistor (0.25W)
  27 Ω Resistor: A generic resistor (0.25W)
  HC-SR501 Body Sensor Module: Pyroelectric Infrared PIR Motion Sensor Detector Module
